// Logisim project Exercicio 1 CIRCUITO 2.circ as structural Verilog: 1 circuit, main circuit main
module main (
  input  A,
  input  B,
  input  C,
  input  D,
  input  E,
  output out_6
);

  wire and_1_out, not_1_out, or_1_out, or_2_out;

  or or_1 (or_1_out, A, B);
  and and_1 (and_1_out, or_1_out, C);
  not not_1 (not_1_out, and_1_out);
  or or_2 (or_2_out, not_1_out, D);
  and and_2 (out_6, or_2_out, E);
endmodule
