// Logisim project Exercicio 3.circ as structural Verilog: 1 circuit, main circuit main
module main (
  input  A,
  input  B,
  output out_3
);

  wire and_1_out, and_2_out, not_1_out;

  not not_1 (not_1_out, B);
  and and_1 (and_1_out, A, B);
  and and_2 (and_2_out, A, not_1_out);
  or or_1 (out_3, and_1_out, and_2_out);
endmodule
