// Logisim project Exercicio 4.circ as structural Verilog: 1 circuit, main circuit main
module main (
  input  Fogo,
  input  F_Energia,
  input  \Vaz_Gás ,
  output Alarme
);

  wire and_1_out;

  and and_1 (and_1_out, F_Energia, \Vaz_Gás );
  or or_1 (Alarme, Fogo, and_1_out);
endmodule
