// Logisim project Q1 letra B.circ as structural Verilog: 1 circuit, main circuit main
module main (
  input  A,
  input  B,
  input  A_2,
  output out_4
);

  wire or_1_out;

  or or_1 (or_1_out, A, B);
  and and_1 (out_4, or_1_out, A_2);
endmodule
