// Logisim project Q2 letra B.circ as structural Verilog: 1 circuit, main circuit main
module main (
  input  A,
  input  B,
  input  C,
  output out_4
);

  wire and_1_out;

  and and_1 (and_1_out, B, C);
  or or_1 (out_4, A, and_1_out);
endmodule
