// Logisim project Q3.circ as structural Verilog: 1 circuit, main circuit main
module main (
  input  A,
  input  B,
  input  C,
  input  A_2,
  input  C_2,
  input  D,
  output out_7
);

  wire and_1_out, and_2_out, not_1_out;

  not not_1 (not_1_out, A_2);
  and and_1 (and_1_out, A, B, C);
  and and_2 (and_2_out, not_1_out, C_2, D);
  or or_1 (out_7, and_1_out, and_2_out);
endmodule
