// Logisim project Q4.circ as structural Verilog: 1 circuit, main circuit main
module main (
  input  Sensor_de_RPM,
  input  \Sensor_de_Pressão ,
  input  Sensor_de_Temperatura,
  output \W__Luz_de_advertência 
);

  wire not_1_out, or_1_out;

  not not_1 (not_1_out, Sensor_de_RPM);
  or or_1 (or_1_out, not_1_out, \Sensor_de_Pressão );
  and and_1 (\W__Luz_de_advertência , or_1_out, Sensor_de_Temperatura);
endmodule
