// Logisim project Q5.circ as structural Verilog: 1 circuit, main circuit main
module main (
  input  Chave_C,
  input  Chave_D,
  input  Chave_B,
  input  Chave_D_2,
  output \Expressão_Final 
);

  wire and_1_out, and_2_out, not_1_out, not_2_out;

  and and_1 (and_1_out, Chave_C, Chave_D);
  not not_1 (not_1_out, and_1_out);
  and and_2 (and_2_out, Chave_B, Chave_D_2);
  not not_2 (not_2_out, and_2_out);
  and and_3 (\Expressão_Final , not_1_out, not_2_out);
endmodule
