// Logisim project Q6.circ as structural Verilog: 1 circuit, main circuit main
module main (
  input  M,
  input  F1,
  input  F2,
  input  F3,
  output OPEN
);

  wire not_1_out, or_1_out;

  not not_1 (not_1_out, M);
  or or_1 (or_1_out, F1, F2, F3);
  and and_1 (OPEN, not_1_out, or_1_out);
endmodule
